# Fritzing sketch Untitled Sketch (saved by Fritzing 1.0.4)
breadboards: 1

parts:
  A1 = Particle - Photon2
  OLED_I2C1 = OLED 128x64 I2C Monochrome Display
  GY1 = MPU-6050 Board GY-521 [form="♀ (female)" package=THT]
  Part1 = Adafruit PA1010D Mini GPS Module [part_number="Adafruit #4415"]
  U1 = LIPO-1000mAh [package=lipo-1000]  # not connected
  HC-SR04_Sensor_1 = HC-SR04 Ultrasonic Distance Sensor
  Part2 = NeoPixel Stick [part_number=1426]

nets:
  VCC: A1.Pin_2, A1.Pin_31, OLED_I2C1.VDD, GY1.pin2, Part1.VCC, HC-SR04_Sensor_1.VCC
  GND: A1.Pin_4, A1.Pin_30, A1.Pin_32, OLED_I2C1.GND, GY1.pin1, Part1.GND, HC-SR04_Sensor_1.GND, Part2.DATAIN
  N1: A1.Pin_9, HC-SR04_Sensor_1.TRIG
  N2: A1.Pin_10, HC-SR04_Sensor_1.ECHO
  N3: A1.Pin_17, OLED_I2C1.SDA, GY1.pin4, Part1.SDA
  N4: A1.Pin_18, OLED_I2C1.SCK, GY1.pin3, Part1.SCL
  N5: A1.Pin_19, Part2.GND
  N6: A1.Pin_26, Part2.+5V

custom parts:
  Particle - Photon2: The Photon 2 is a microcontroller and Wi-Fi networking developed by particle. Features: 802.11a/b/g/n Wi-Fi, 2.4 GHz and 5 GHz Integrated PCB antenna Integrated U.FL connector for external antenna Integrated RF switch BLE 5 using same antenna as Wi-Fi Realtek RTL8721DM MCU ARM Cortex M33 CPU, 200 MHz 2048 KB (2 MB) user application maximum size 3072 KB (3 MB) of RAM available to user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
  MPU-6050 Board GY-521: Acelerometro y Giroscopio MPU-6050 Board GY-521
  Adafruit PA1010D Mini GPS Module: This miniature GPS breakout is only 1" x 1" (~ 25mm x 25mm) but houses a complete GPS/GNSS solution with both I2C and UART interfaces. There's even an antenna on top so it's plug and play! Support for GPS, GLONASS, GALILEO, QZSS -165 dBm sensitivity, up to 10 Hz updates Up to 210 PRN channels with 99 search channels and 33 simultaneous tracking channels 5V friendly design and only 30mA current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
  NeoPixel Stick: Make your own little LED strip arrangement with this stick of NeoPixel LEDs. We crammed 8 of the tiny 5050 (5mm x 5mm) smart RGB LEDs onto a PCB with mounting holes and a chainable design. Use only one microcontroller pin to control as many as you can chain together! Each LED is addressable as the driver chip is inside the LED. Each one has ~18mA constant current drive so the color will be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
